# Fritzing sketch tricolorLEDProtoBoardLayout1 (saved by Fritzing 0.9.4)
breadboards: 1

parts:
  Teensy_v3_2 = Teensy 3.1  # not connected
  Tri-Colour_LED = RGB LED (com. cathode, rgb) [package="5 mm [THT]"]
  220-Ohm_Resistor_(Green) = Resistor [tolerance=±5% resistance=220 package="2512 [SMD]"]
  220-Ohm_Resistor_(Blue) = Resistor [tolerance=±5% resistance=220 package="2512 [SMD]"]
  220-Ohm_Resistor_(Red) = Resistor [tolerance=±5% resistance=220 package="2512 [SMD]"]

nets:
  N1: Tri-Colour_LED.red_anode, 220-Ohm_Resistor_(Red).Pin_0
  N2: Tri-Colour_LED.common_cathode, 220-Ohm_Resistor_(Blue).Pin_0
  N3: Tri-Colour_LED.blue_anode, 220-Ohm_Resistor_(Green).Pin_0

notes:
  CST8227 - Interfacing
  Lab 03 - PWM
  Tri-colour LED: Red, Green, Blue (RGB)
  Notes:
  * use PWM pins on the Teensy
  * this circuit is for Demos #1 and #2; you'll need to add a push-button switch (PBS) for Demos #3 and #4.
  Gerald.Hurdle@AlgonquinCollege.com
