# Fritzing sketch lab4 (saved by Fritzing 0.9.4)
breadboards: 1

parts:
  Teensy_v3_3 = Teensy 3.1  # not connected
  LED1 = RGB LED - (4 legs) [package="5 mm [THT]"]
  220-Ohm_Resistor_(Green)1 = Resistor [tolerance=±5% resistance=220 package="2512 [SMD]"]
  220-Ohm_Resistor_(Blue)1 = Resistor [tolerance=±5% resistance=220 package="2512 [SMD]"]
  220-Ohm_Resistor_(Red)1 = Resistor [tolerance=±5% resistance=220 package="2512 [SMD]"]
  R1 = Resistor [tolerance=±1% resistance=10k package=THT]
  S2 = Pushbutton [package="[THT]"]
  S3 = Pushbutton [package="[THT]"]

nets:
  N1: LED1.red_cathode, 220-Ohm_Resistor_(Red)1.Pin_0
  N2: LED1.common_anode, 220-Ohm_Resistor_(Blue)1.Pin_0
  N3: LED1.green_cathode, S2.Pin_1, S2.Pin_2, S3.Pin_1, S3.Pin_2
  N4: LED1.blue_cathode, 220-Ohm_Resistor_(Green)1.Pin_0
  N5: R1.Pin_1, S2.Pin_3, S2.Pin_4
  N6: S3.Pin_3, S3.Pin_4

notes:
  Name: Rutvik Patel
  Student No: 040915445
  College ID: pate0635@algonquinlive.com
  Lab: 4
