# Fritzing sketch 1 (saved by Fritzing 0.9.4)
breadboards: 1

parts:
  Teensy_v3_2 = Teensy 3.1  # not connected
  Tri-Colour_LED = RGB LED (com. cathode, rgb) [package="5 mm [THT]"]
  220-Ohm_Resistor_(Green) = Resistor [tolerance=±5% resistance=220 package="2512 [SMD]"]
  220-Ohm_Resistor_(Blue) = Resistor [tolerance=±5% resistance=220 package="2512 [SMD]"]
  220-Ohm_Resistor_(Red) = Resistor [tolerance=±5% resistance=220 package="2512 [SMD]"]
  R1 = Trimmer Potentiometer [maximum_resistance=10kΩ package=THT]

nets:
  N1: Tri-Colour_LED.red_anode, 220-Ohm_Resistor_(Red).Pin_0
  N2: Tri-Colour_LED.common_cathode, 220-Ohm_Resistor_(Blue).Pin_0
  N3: Tri-Colour_LED.green_anode, R1.leg1
  N4: Tri-Colour_LED.blue_anode, 220-Ohm_Resistor_(Green).Pin_0

notes:
  CST8227 - Interfacing
  Lab 06 - User Controlled LED Color
  Use Potentiometer as user input to control LED colour.
  040915445
  @author Rutvik Patel
  (pate0635@algonquinlive.com)
